# Fritzing sketch TimeBomb (saved by Fritzing 0.9.4)
breadboards: 1

parts:
  Part1 = Arduino Uno (Rev3) - ICSP
  Part2 = OLED Monochrome 128x64 1.3 inch [part_number=938]
  S1 = Pushbutton [package="[THT]"]
  R1 = Resistor [tolerance=±5% resistance=220 package=THT]
  R2 = Resistor [tolerance=±5% resistance=10k package="0805 [SMD]"]
  R3 = Resistor [tolerance=±5% resistance=220 package=THT]
  R4 = Resistor [tolerance=±5% resistance=10k package="0805 [SMD]"]
  R5 = Resistor [tolerance=±5% resistance=10k package="0805 [SMD]"]
  LED1 = LED - 3mm [color="Green (555nm)" package="3 mm [THT]"]
  LED2 = LED - 3mm [color="Red (633nm)" package="3 mm [THT]"]

nets:
  5V: Part1.5V, Part2.VIN, R4.Pin_0, R5.Pin_0
  N1: Part1.ICSP_MOSI, Part1.D11_PWM/MOSI, Part2.DC_SA0
  N2: Part1.D9_PWM, Part2.MOSI_SDA
  N3: Part1.D10_PWM/SS, Part2.SCLK_SCK
  N4: Part1.D12/MISO, Part2.RESET
  N5: Part1.D13/SCK, Part2.CS
  GND: Part1.GND, Part2.GND, R1.Pin_0, R2.Pin_0, R3.Pin_0
  N6: Part1.D2, S1.Pin_3, S1.Pin_4, R2.Pin_1
  N7: Part1.D3_PWM, LED1.cathode
  N8: Part1.D4, LED2.cathode
  N9: Part1.D6_PWM, R4.Pin_1
  N10: Part1.D7, R5.Pin_1
  N11: S1.Pin_1, S1.Pin_2
  N12: R1.Pin_1, LED1.anode
  N13: R3.Pin_1, LED2.anode

custom parts:
  OLED Monochrome 128x64 1.3 inch: These displays are small, only about 1.3" diagonal, but very readable due to the high contrast of an OLED display. This display is made of 128x64 individual white OLED pixels, each one is turned on or off by the controller chip. Because the display makes its own light, no backlight is required. This reduces the power required to run the OLED and is why the display has such high contrast; we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
